# Fritzing sketch Buzzer_with_push_button (saved by Fritzing 0.9.4)
breadboards: 1

parts:
  Part1 = Arduino Uno (Rev3)
  J1 = Piezo Speaker
  S1 = Momentary Switch [package=ksa_sealed_tac_switch]

nets:
  N1: Part1.D8, J1.pin2
  N2: Part1.D7, S1.3
  N3: Part1.GND, J1.pin1, S1.2
